# Fritzing sketch Untitled Sketch (saved by Fritzing 0.8.7b)

parts:
  Part1 = Arduino Uno (Rev3)
  M1 = Stepper Motor - Bipolar  # not connected
  S1 = H-Bridge with L298N
  Power_plug1 = Power plug

nets:
  N1: Part1.D8, S1.IN4
  N2: Part1.D9_PWM, S1.IN3
  N3: Part1.D10_PWM/SS, S1.IN2
  N4: Part1.D11_PWM/MOSI, S1.IN1
  GND: Part1.GND, S1.GND, Power_plug1.GND
  5V: S1.5V, Power_plug1.VCC

custom parts:
  H-Bridge with L298N: h-bridge
